# Fritzing sketch Ellipal-Joy-Nucleo (saved by Fritzing 0.9.10b)
breadboards: 1

parts:
  M1 = Nucleo 144 MB1137
  o1 = Module display OLED I2C 128x64 SSD1306 [package=THT]
  S1 = Pushbutton [package="[SMD]"]
  S2 = Pushbutton [package="[SMD]"]
  S3 = Pushbutton [package="[SMD]"]
  S4 = Pushbutton [package="[SMD]"]

nets:
  +3.3V: M1.+3.3V, o1.VCC, S1.Pin_1, S1.Pin_2, S2.Pin_1, S2.Pin_2, S3.Pin_1, S3.Pin_2, S4.Pin_3, S4.Pin_4
  GND: M1.GND, o1.GND
  N1: M1.PG9, M1.USART_A_RX_/PG9, o1.SDA
  N2: M1.TIMER_A_PWM3N/PE12, M1.PE12, S4.Pin_1, S4.Pin_2
  N3: M1.PD!!, S3.Pin_3, S3.Pin_4
  N4: M1.PD12, S2.Pin_3, S2.Pin_4
  N5: M1.PD13, S1.Pin_3, S1.Pin_4
  N6: M1.USART_A_TX_/PG14, M1.PG14, o1.SCL

notes:
  Key1
  Key2
  Charge

custom parts:
  Nucleo 144 MB1137: The STM32 Nucleo-144 boards based on the MB1137 reference board (NUCLEO-F207ZG, NUCLEO-F303ZE, NUCLEO-F412ZG, NUCLEO-F413ZH, NUCLEO-F429ZI, NUCLEO-F439ZI, NUCLEO-F446ZE, NUCLEO-F722ZE, NUCLEO-F746ZG, NUCLEO-F756ZG, NUCLEO-F767ZI and NUCLEO-H743ZI) provide an affordable and flexible way for users to try out new concepts and build prototypes with STM32 microcontrollers.
  Module display OLED I2C 128x64 SSD1306: Ecran OLED I2C SSD163 de 128x64 avec connexion I2C
